// Logisim project s-mips.circ as structural Verilog: 16 circuits, main circuit S-MIPS Board
module S_MIPS_Board (
  input  DESHABILITAR_DISPATCHER,
  output halt
);

  wire button_1_out, CLK, CS, d_ff_1_q, LCLR, LoadRAM, LoadRAMOn, LW, R_R_W, R_W, ram_dispatcher_1_finished,
       RCS, Reset_out, RST, TTY_EN;
  wire [2:0] KDB;
  wire [3:0] LMask, Mask, ram_1_read_time, ram_1_write_time, RMask;
  wire [6:0] KDB_DATA, TTY_DATA;
  wire [15:0] Addr, LAddr, RAddr;
  wire [31:0] I0, I1, I2, I3, LData, ram_1_data_out_0, ram_1_data_out_1, ram_1_data_out_2, ram_1_data_out_3,
       RI0, RI1, RI2, RI3;

  TTY #(.rows(25), .cols(80)) tty_1 (.data(TTY_DATA), .clk(CLK), .we(TTY_EN), .clr(RST));
  not not_1 (LoadRAMOn, ram_dispatcher_1_finished);
  RAM_Dispatcher ram_dispatcher_1 (
    .WriteTime(ram_1_write_time), .Clock(CLK), .Data(LData), .Address(LAddr), .Mask(LMask),
    .Finished(ram_dispatcher_1_finished), .Write(LW), .CLR(LCLR));
  Keyboard #(.buflen(64)) keyboard_1 (.clk(CLK), .re(KDB[0]), .avail(KDB[2]), .data(KDB_DATA));  // open: clr
  RAM ram_1 (
    .Address(RAddr), .Data_Out_0(ram_1_data_out_0), .Data_Out_1(ram_1_data_out_1),
    .Data_Out_2(ram_1_data_out_2), .Data_Out_3(ram_1_data_out_3), .Data_In_0(RI0), .Data_In_1(RI1),
    .Data_In_2(RI2), .Data_In_3(RI3), .Mask(RMask), .nRead_Write(R_R_W), .Chip_Select(RCS),
    .Read_Time(ram_1_read_time), .Reset(button_1_out), .Write_Time(ram_1_write_time));
  Button button_1 (.out(button_1_out));
  D_Flip_Flop d_ff_1 (.clk(CLK), .D(1'b1), .Q(d_ff_1_q), .reset(Reset_out));  // open: Qn, preset, en
  Button Reset (.out(Reset_out));
  S_MIPS s_mips_1 (
    .Kbd_Enable(KDB[0]), .Address(Addr), .Kbd_Clear(KDB[1]), .Kbd_Available(KDB[2]), .RAM_In_0(I0),
    .Kbd_ASCII_Data(KDB_DATA), .RAM_In_1(I1), .TTY_Enable(TTY_EN), .RAM_In_2(I2), .RAM_In_3(I3),
    .TTY_ASCII_Data(TTY_DATA), .Reset(RST), .RAM_Out_0(ram_1_data_out_0), .Clock(CLK),
    .RAM_Out_1(ram_1_data_out_1), .Stop(halt), .RAM_Out_2(ram_1_data_out_2), .RAM_Out_3(ram_1_data_out_3),
    .Mask(Mask), .Read_Time(ram_1_read_time), .Write_Time(ram_1_write_time), .nRead_Write(R_W),
    .Chip_Select(CS));
  D_Flip_Flop d_ff_2 (.clk(CLK), .D(d_ff_1_q), .Qn(LCLR), .reset(Reset_out));  // open: Q, preset, en
  or or_1 (RST, LCLR, LoadRAM);
  Clock clock_1 (.out(CLK));
  Multiplexer #(.width(32), .enable("false")) multiplexer_1 (.in0(I0), .in1(LData), .out(RI0), .sel(LoadRAM));
  Multiplexer #(.width(32), .enable("false")) multiplexer_2 (.in0(I1), .in1(LData), .out(RI1), .sel(LoadRAM));
  Multiplexer #(.width(32), .enable("false")) multiplexer_3 (.in0(I2), .in1(LData), .out(RI2), .sel(LoadRAM));
  Multiplexer #(.width(32), .enable("false")) multiplexer_4 (.in0(I3), .in1(LData), .out(RI3), .sel(LoadRAM));
  and and_1 (LoadRAM, ~DESHABILITAR_DISPATCHER, LoadRAMOn);  // AND_Gate
  Multiplexer #(.width(16), .enable("false")) multiplexer_5 (.in0(Addr), .in1(LAddr), .out(RAddr), .sel(LoadRAM));
  Multiplexer #(.width(4), .enable("false")) multiplexer_6 (.in0(Mask), .in1(LMask), .out(RMask), .sel(LoadRAM));
  Multiplexer #(.enable("false")) multiplexer_7 (.in0(CS), .in1(LW), .out(RCS), .sel(LoadRAM));
  Multiplexer #(.enable("false")) multiplexer_8 (.in0(R_W), .in1(LW), .out(R_R_W), .sel(LoadRAM));

  // Notes on the sheet:
  //   NO MODIFICAR
  //   Keyboard
endmodule

module RAM (
  input  [15:0] Address,
  input  [31:0] Data_In_0,
  input  [31:0] Data_In_1,
  input  [31:0] Data_In_2,
  input  [31:0] Data_In_3,
  input  [3:0] Mask,
  input  nRead_Write,
  input  Chip_Select,
  input  Reset,
  output [31:0] Data_Out_0,
  output [31:0] Data_Out_1,
  output [31:0] Data_Out_2,
  output [31:0] Data_Out_3,
  output [3:0] Read_Time,
  output [3:0] Write_Time
);

  wire and_2_out, and_3_out, and_4_out, and_5_out, and_6_out, and_7_out, and_8_out, and_9_out, Changed, CLK,
       comparator_2_eq, comparator_3_eq, comparator_4_eq, comparator_5_eq, comparator_6_eq, Count,
       demultiplexer_3_out0, Idle, Idle_q, Load, Load0, Load1, nand_1_out, or_1_out, or_2_out, or_3_out,
       or_4_out, or_5_out, or_6_out, or_7_out, or_8_out, or_9_out, or_10_out, Proc_q, Update_Mem, Zero_Time;
  wire [3:0] counter_1_q, multiplexer_1_out, subtractor_1_out;
  wire [31:0] register_1_q, register_2_q, register_3_q, register_4_q, register_5_q;

  // Probe on 4'b0011
  // Probe on 4'b0010
  Multiplexer #(.width(4), .enable("false")) multiplexer_1 (
    .in0(4'b0011), .in1(4'b0010), .out(multiplexer_1_out), .sel(nRead_Write));
  or or_1 (or_1_out, Idle, Update_Mem);
  or or_2 (or_2_out, ~Chip_Select, Reset);  // OR_Gate
  Subtractor #(.width(4)) subtractor_1 (.a(multiplexer_1_out), .b(4'b0010), .out(subtractor_1_out));  // open: bin, bout
  D_Flip_Flop u_Idle (.clk(CLK), .D(or_1_out), .Q(Idle_q), .preset(or_2_out));  // open: Qn, en, reset
  Demultiplexer #(.enable("false")) demultiplexer_1 (.out0(Idle), .out1(Load0), .in(Idle_q), .sel(Changed));
  // Probe on counter_1_q
  Counter #(.width(4), .max('hf)) counter_1 (
    .load(Load), .D(subtractor_1_out), .count(Count), .Q(counter_1_q), .clk(CLK), .clr(or_3_out));  // open: carry
  or or_3 (or_3_out, ~Chip_Select, Reset);  // OR_Gate
  Comparator #(.width(4), .mode("unsigned")) comparator_1 (
    .a(4'b0000), .b(counter_1_q), .eq(Zero_Time));  // open: gt, lt
  or or_4 (or_4_out, Count, Load0, Load1);
  Register #(.width(32)) register_1 (.D(Data_In_0), .en(Chip_Select), .Q(register_1_q), .clk(CLK), .clr(or_5_out));
  or or_5 (or_5_out, ~Chip_Select, Reset);  // OR_Gate
  Register #(.width(32)) register_2 (.D(Data_In_1), .en(Chip_Select), .Q(register_2_q), .clk(CLK), .clr(or_6_out));
  or or_6 (or_6_out, ~Chip_Select, Reset);  // OR_Gate
  Register #(.width(32)) register_3 (.D(Data_In_2), .en(Chip_Select), .Q(register_3_q), .clk(CLK), .clr(or_7_out));
  or or_7 (or_7_out, ~Chip_Select, Reset);  // OR_Gate
  Register #(.width(32)) register_4 (.D(Data_In_3), .en(Chip_Select), .Q(register_4_q), .clk(CLK), .clr(or_8_out));
  or or_8 (or_8_out, ~Chip_Select, Reset);  // OR_Gate
  Register #(.width(32)) register_5 (
    .D({{11{1'b1}}, nRead_Write, Mask, Address}), .en(Chip_Select), .Q(register_5_q), .clk(CLK),
    .clr(or_9_out));
  or or_9 (or_9_out, ~Chip_Select, Reset);  // OR_Gate
  D_Flip_Flop Proc (.clk(CLK), .D(or_4_out), .Q(Proc_q), .reset(or_10_out));  // open: Qn, preset, en
  or or_10 (or_10_out, ~Chip_Select, Reset);  // OR_Gate
  Demultiplexer #(.enable("false")) demultiplexer_2 (
    .out0(Count), .out1(Update_Mem), .in(demultiplexer_3_out0), .sel(Zero_Time));
  Demultiplexer #(.enable("false")) demultiplexer_3 (
    .out0(demultiplexer_3_out0), .out1(Load1), .in(Proc_q), .sel(Changed));
  Clock clock_1 (.out(CLK));
  Comparator #(.width(32)) comparator_2 (.a(register_1_q), .b(Data_In_0), .eq(comparator_2_eq));  // open: gt, lt
  Comparator #(.width(32)) comparator_3 (.a(register_2_q), .b(Data_In_1), .eq(comparator_3_eq));  // open: gt, lt
  Comparator #(.width(32)) comparator_4 (.a(register_3_q), .b(Data_In_2), .eq(comparator_4_eq));  // open: gt, lt
  Comparator #(.width(32)) comparator_5 (.a(register_4_q), .b(Data_In_3), .eq(comparator_5_eq));  // open: gt, lt
  Comparator #(.width(32)) comparator_6 (
    .a(register_5_q), .b({{11{1'b1}}, nRead_Write, Mask, Address}), .eq(comparator_6_eq));  // open: gt, lt
  nand nand_1 (nand_1_out, comparator_6_eq, comparator_2_eq, comparator_3_eq, comparator_4_eq, comparator_5_eq);
  and and_1 (Changed, nand_1_out, Chip_Select);
  or or_11 (Load, Count, Load1, Load0);
  and and_2 (and_2_out, Mask[0], Update_Mem, nRead_Write);
  and and_3 (and_3_out, Mask[1], Update_Mem, nRead_Write);
  and and_4 (and_4_out, Mask[2], Update_Mem, nRead_Write);
  and and_5 (and_5_out, Mask[3], Update_Mem, nRead_Write);
  RAM_part #(.addrWidth(16), .dataWidth(32), .bus("separate")) ram_1 (
    .addr(Address), .din(Data_In_0), .data(Data_Out_0), .str(and_2_out), .sel(Chip_Select), .clk(CLK),
    .ld(and_6_out), .clr(Reset));
  and and_6 (and_6_out, ~nRead_Write, Idle);  // AND_Gate
  RAM_part #(.addrWidth(16), .dataWidth(32), .bus("separate")) ram_2 (
    .addr(Address), .din(Data_In_1), .data(Data_Out_1), .str(and_3_out), .sel(Chip_Select), .clk(CLK),
    .ld(and_7_out), .clr(Reset));
  and and_7 (and_7_out, ~nRead_Write, Idle);  // AND_Gate
  RAM_part #(.addrWidth(16), .dataWidth(32), .bus("separate")) ram_3 (
    .addr(Address), .din(Data_In_2), .data(Data_Out_2), .str(and_4_out), .sel(Chip_Select), .clk(CLK),
    .ld(and_8_out), .clr(Reset));
  and and_8 (and_8_out, ~nRead_Write, Idle);  // AND_Gate
  RAM_part #(.addrWidth(16), .dataWidth(32), .bus("separate")) ram_4 (
    .addr(Address), .din(Data_In_3), .data(Data_Out_3), .str(and_5_out), .sel(Chip_Select), .clk(CLK),
    .ld(and_9_out), .clr(Reset));
  and and_9 (and_9_out, ~nRead_Write, Idle);  // AND_Gate

  assign Read_Time = 4'b0011;
  assign Write_Time = 4'b0010;

  // Other names for the same wires on the sheet: M0 = Mask[0]; M1 = Mask[1]; M2 = Mask[2]; M3 = Mask[3];
  //   RW = nRead_Write; CLR = Reset; CS = Chip_Select; Load2 = Count

  // Notes on the sheet:
  //   NO MODIFICAR
  //   excepto quizás los valores RT y WT
  //   BANK0
  //   BANK1
  //   BANK2
  //   BANK3
endmodule

module S_MIPS (
  input  Kbd_Available,
  input  [6:0] Kbd_ASCII_Data,
  input  [31:0] RAM_Out_0,
  input  [31:0] RAM_Out_1,
  input  Reset,
  input  [31:0] RAM_Out_2,
  input  Clock,
  input  [31:0] RAM_Out_3,
  input  [3:0] Read_Time,
  input  [3:0] Write_Time,
  output Kbd_Enable,
  output [15:0] Address,
  output Kbd_Clear,
  output TTY_Enable,
  output [6:0] TTY_ASCII_Data,
  output Stop,
  output [31:0] RAM_In_0,
  output [31:0] RAM_In_1,
  output [31:0] RAM_In_2,
  output [31:0] RAM_In_3,
  output [3:0] Mask,
  output nRead_Write,
  output Chip_Select
);


  // Other names for the same wires on the sheet: CLK = Clock; CLR = Reset; CS = Chip_Select;
  //   KBD_AVAIL = Kbd_Available; KBD_CLR = Kbd_Clear; KBD_DATA[6:0] = Kbd_ASCII_Data; RAM_A[15:0] = Address;
  //   RAM_INPUT_0[31:0] = RAM_In_0; RAM_INPUT_1[31:0] = RAM_In_1; RAM_INPUT_2[31:0] = RAM_In_2;
  //   RAM_INPUT_3[31:0] = RAM_In_3; RAM_MASK[3:0] = Mask; RAM_OUTPUT_0[31:0] = RAM_Out_0;
  //   RAM_OUTPUT_1[31:0] = RAM_Out_1; RAM_OUTPUT_2[31:0] = RAM_Out_2; RAM_OUTPUT_3[31:0] = RAM_Out_3;
  //   RW = nRead_Write; TTY_DATA[6:0] = TTY_ASCII_Data

  // Notes on the sheet:
  //   RAM ADDRESS
  //   DATA FROM RAM
  //   DATA TO RAM
  //   DATA WRITE MASK
  //   RAM TIMING
  //   RAM CONTROL
  //   KEYBOARD
  //   TTY
  //   SEQUENCING
endmodule

module RAM_Dispatcher (
  input  [3:0] WriteTime,
  input  Clock,
  input  CLR,
  output [31:0] Data,
  output [15:0] Address,
  output [3:0] Mask,
  output Finished,
  output Write
);

  wire demultiplexer_2_out1, demultiplexer_3_out1, End, IDLE_q, IncAddr, Load, or_1_out, or_2_out, While_q,
       WriteEnd;
  wire [3:0] counter_1_q;
  wire [31:0] CurrentAddress_q;

  Counter #(.width(32), .max('hffffffff)) CurrentAddress (
    .count(IncAddr), .Q({CurrentAddress_q[31:18], Address, CurrentAddress_q[1:0]}), .clk(Clock), .clr(CLR));  // open: load, D, carry
  or or_1 (or_1_out, IncAddr, demultiplexer_3_out1, Finished);
  D_Flip_Flop IDLE (.clk(Clock), .D(or_1_out), .Q(IDLE_q), .preset(CLR));  // open: Qn, en, reset
  Demultiplexer #(.enable("false")) demultiplexer_1 (.out0(Load), .out1(Finished), .in(IDLE_q), .sel(End));
  D_Flip_Flop While (.clk(Clock), .D(or_2_out), .Q(While_q), .reset(CLR));  // open: Qn, preset, en
  or or_2 (or_2_out, Write, Load);
  RAM_part #(.addrWidth(18), .dataWidth(32)) ram_1 (
    .addr({Address, CurrentAddress_q[1:0]}), .data(Data), .clk(Clock));  // open: sel, ld, clr
  Demultiplexer #(.enable("false")) demultiplexer_2 (
    .out0(Write), .out1(demultiplexer_2_out1), .in(While_q), .sel(WriteEnd));
  Decoder #(.select(2)) decoder_1 (
    .out0(Mask[0]), .out1(Mask[1]), .out2(Mask[2]), .out3(Mask[3]), .sel(CurrentAddress_q[1:0]));  // open: en
  Demultiplexer #(.enable("false")) demultiplexer_3 (
    .out0(IncAddr), .out1(demultiplexer_3_out1), .in(demultiplexer_2_out1), .sel(End));
  Counter #(.width(4), .max('hf)) counter_1 (
    .load(Load), .D(WriteTime), .count(Write), .Q(counter_1_q), .clk(Clock));  // open: carry, clr
  Comparator #(.width(32)) comparator_1 (.a(Data), .b({32{1'b1}}), .eq(End));  // open: gt, lt
  Comparator #(.width(4)) comparator_2 (.a(4'b0000), .b(counter_1_q), .eq(WriteEnd));  // open: gt, lt

  // Other names for the same wires on the sheet: CLK = Clock; Count = Write; WT[3:0] = WriteTime
endmodule

module Operation_Decoder (
  input  [5:0] in_1,
  input  [5:0] in_2,
  input  in_3,
  input  in_4,
  input  in_5,
  output [3:0] ALU_Slc,
  output [1:0] BC_Slc,
  output Extend_Slc,
  output Arit,
  output Copia,
  output Pila,
  output Salto,
  output Arit_I,
  output Especial,
  output Load_Word,
  output Store_Word
);

  wire _11_1111, add, addi, \and , and_1_out, and_2_out, and_15_out, and_16_out, and_17_out, and_18_out,
       and_19_out, andi, beq, bgtz, blez, bltz, bne, comparator_2_eq, comparator_3_eq, comparator_4_eq,
       comparator_5_eq, comparator_6_eq, comparator_7_eq, comparator_8_lt, comparator_9_eq, comparator_9_gt,
       comparator_10_lt, comparator_11_gt, comparator_12_lt, comparator_13_gt, comparator_15_eq,
       comparator_16_eq, comparator_17_eq, comparator_18_eq, comparator_20_eq, comparator_21_eq,
       comparator_22_eq, comparator_23_eq, comparator_24_eq, comparator_25_eq, comparator_26_eq,
       comparator_27_eq, comparator_28_eq, comparator_29_eq, comparator_30_eq, comparator_31_eq, div, divu,
       halt, j, jr, kbd, mfhi, mflo, mult, mulu, nop, \nor , \or , or_3_out, ori, pop, push, rnd, Rs__0_t,
       Rs___0, Rs____Rt, slt, slti, sltiu, sltu, sub, tty, \xor , xori;

  Comparator #(.width(6)) comparator_1 (.a(in_1), .b({6{1'b0}}), .eq(Especial));  // open: gt, lt
  Comparator #(.width(6)) comparator_2 (.a(in_2), .b(6'b100000), .eq(comparator_2_eq));  // open: gt, lt
  Comparator #(.width(6)) comparator_3 (.a(in_2), .b(6'b100010), .eq(comparator_3_eq));  // open: gt, lt
  Comparator #(.width(6)) comparator_4 (.a(in_2), .b(6'b011000), .eq(comparator_4_eq));  // open: gt, lt
  Comparator #(.width(6)) comparator_5 (.a(in_2), .b(6'b011001), .eq(comparator_5_eq));  // open: gt, lt
  Comparator #(.width(6)) comparator_6 (.a(in_2), .b(6'b011010), .eq(comparator_6_eq));  // open: gt, lt
  Comparator #(.width(6)) comparator_7 (.a(in_2), .b(6'b011011), .eq(comparator_7_eq));  // open: gt, lt
  or or_1 (Rs___0, in_3, in_4);
  not not_1 (Rs__0_t, Rs___0);
  not not_2 (Rs____Rt, in_5);
  Comparator #(.width(6)) comparator_8 (.a(in_1), .b(6'b001000), .lt(comparator_8_lt));  // open: gt, eq
  and and_1 (and_1_out, comparator_8_lt, comparator_9_gt);
  Comparator #(.width(6)) comparator_9 (
    .a(in_1), .b({6{1'b0}}), .gt(comparator_9_gt), .eq(comparator_9_eq));  // open: lt
  and and_2 (and_2_out, comparator_9_eq, comparator_10_lt);
  Comparator #(.width(6)) comparator_10 (.a(in_2), .b(6'b001001), .lt(comparator_10_lt));  // open: gt, eq
  Comparator #(.width(6)) comparator_11 (.a(in_2), .b(6'b001111), .gt(comparator_11_gt));  // open: eq, lt
  Comparator #(.width(6)) comparator_12 (.a(in_2), .b(6'b010011), .lt(comparator_12_lt));  // open: gt, eq
  Comparator #(.width(6)) comparator_13 (.a(in_2), .b(6'b010111), .gt(comparator_13_gt));  // open: eq, lt
  and and_3 (add, Especial, comparator_2_eq);
  and and_4 (sub, Especial, comparator_3_eq);
  and and_5 (mult, Especial, comparator_4_eq);
  and and_6 (mulu, Especial, comparator_5_eq);
  and and_7 (div, Especial, comparator_6_eq);
  and and_8 (divu, Especial, comparator_7_eq);
  or or_2 (Salto, and_1_out, and_2_out);
  and and_9 (Copia, comparator_9_eq, comparator_11_gt, comparator_12_lt);
  and and_10 (Arit, comparator_9_eq, comparator_13_gt);
  Comparator #(.width(6)) comparator_14 (.a(in_1), .b({6{1'b1}}), .eq(_11_1111));  // open: gt, lt
  and and_11 (\and , Especial, comparator_15_eq);
  Comparator #(.width(6)) comparator_15 (.a(in_2), .b(6'b100100), .eq(comparator_15_eq));  // open: gt, lt
  and and_12 (\or , Especial, comparator_16_eq);
  Comparator #(.width(6)) comparator_16 (.a(in_2), .b(6'b100101), .eq(comparator_16_eq));  // open: gt, lt
  and and_13 (\nor , Especial, comparator_17_eq);
  Comparator #(.width(6)) comparator_17 (.a(in_2), .b(6'b100111), .eq(comparator_17_eq));  // open: gt, lt
  and and_14 (\xor , Especial, comparator_18_eq);
  Comparator #(.width(6)) comparator_18 (.a(in_2), .b(6'b101000), .eq(comparator_18_eq));  // open: gt, lt
  and and_15 (and_15_out, beq, in_5);
  and and_16 (and_16_out, bne, Rs____Rt);
  and and_17 (and_17_out, blez, Rs___0);
  and and_18 (and_18_out, bgtz, Rs__0_t);
  and and_19 (and_19_out, bltz, in_4);
  Comparator #(.width(6)) comparator_19 (.a(in_1), .b(6'b111000), .eq(Pila));  // open: gt, lt
  or or_3 (or_3_out, and_15_out, and_16_out, and_17_out, and_18_out, and_19_out);
  Comparator #(.width(6)) comparator_20 (.a(in_2), .b(6'b101010), .eq(comparator_20_eq));  // open: gt, lt
  Comparator #(.width(6)) comparator_21 (.a(in_2), .b(6'b101011), .eq(comparator_21_eq));  // open: gt, lt
  Comparator #(.width(6)) comparator_22 (.a(in_2), .b(6'b010000), .eq(comparator_22_eq));  // open: gt, lt
  Comparator #(.width(6)) comparator_23 (.a(in_2), .b(6'b010010), .eq(comparator_23_eq));  // open: gt, lt
  Comparator #(.width(6)) comparator_24 (.a(in_2), .b({6{1'b0}}), .eq(comparator_24_eq));  // open: gt, lt
  Comparator #(.width(6)) comparator_25 (.a(in_2), .b(6'b001000), .eq(comparator_25_eq));  // open: gt, lt
  or or_4 (BC_Slc[0], or_3_out, jr);
  or or_5 (BC_Slc[1], jr, j);
  and and_20 (slt, Especial, comparator_20_eq);
  and and_21 (sltu, Especial, comparator_21_eq);
  and and_22 (mfhi, Especial, comparator_22_eq);
  and and_23 (mflo, Especial, comparator_23_eq);
  and and_24 (nop, Especial, comparator_24_eq);
  and and_25 (jr, Especial, comparator_25_eq);
  Comparator #(.width(6)) comparator_26 (.a(in_2), .b({6{1'b1}}), .eq(comparator_26_eq));  // open: gt, lt
  Comparator #(.width(6)) comparator_27 (.a(in_2), .b(6'b000001), .eq(comparator_27_eq));  // open: gt, lt
  Comparator #(.width(6)) comparator_28 (.a(in_2), .b(6'b000010), .eq(comparator_28_eq));  // open: gt, lt
  Comparator #(.width(6)) comparator_29 (.a(in_2), .b(6'b000100), .eq(comparator_29_eq));  // open: gt, lt
  Comparator #(.width(6)) comparator_30 (.a(in_2), .b({6{1'b0}}), .eq(comparator_30_eq));  // open: gt, lt
  Comparator #(.width(6)) comparator_31 (.a(in_2), .b(6'b000001), .eq(comparator_31_eq));  // open: gt, lt
  or or_6 (Extend_Slc, andi, ori, xori);
  and and_26 (halt, _11_1111, comparator_26_eq);
  and and_27 (tty, _11_1111, comparator_27_eq);
  and and_28 (rnd, _11_1111, comparator_28_eq);
  and and_29 (kbd, _11_1111, comparator_29_eq);
  and and_30 (pop, Pila, comparator_30_eq);
  and and_31 (push, Pila, comparator_31_eq);
  Comparator #(.width(6)) comparator_32 (.a(in_1), .b(6'b001000), .eq(addi));  // open: gt, lt
  Comparator #(.width(6)) comparator_33 (.a(in_1), .b(6'b001100), .eq(andi));  // open: gt, lt
  Comparator #(.width(6)) comparator_34 (.a(in_1), .b(6'b001101), .eq(ori));  // open: gt, lt
  Comparator #(.width(6)) comparator_35 (.a(in_1), .b(6'b001110), .eq(xori));  // open: gt, lt
  Comparator #(.width(6)) comparator_36 (.a(in_1), .b(6'b001010), .eq(slti));  // open: gt, lt
  Comparator #(.width(6)) comparator_37 (.a(in_1), .b(6'b001011), .eq(sltiu));  // open: gt, lt
  Comparator #(.width(6)) comparator_38 (.a(in_1), .b(6'b000100), .eq(beq));  // open: gt, lt
  Comparator #(.width(6)) comparator_39 (.a(in_1), .b(6'b000101), .eq(bne));  // open: gt, lt
  Comparator #(.width(6)) comparator_40 (.a(in_1), .b(6'b000110), .eq(blez));  // open: gt, lt
  Comparator #(.width(6)) comparator_41 (.a(in_1), .b(6'b000111), .eq(bgtz));  // open: gt, lt
  Comparator #(.width(6)) comparator_42 (.a(in_1), .b(6'b000001), .eq(bltz));  // open: gt, lt
  Comparator #(.width(6)) comparator_43 (.a(in_1), .b(6'b100011), .eq(Load_Word));  // open: gt, lt
  Comparator #(.width(6)) comparator_44 (.a(in_1), .b(6'b101011), .eq(Store_Word));  // open: gt, lt
  ALU_Encoder alu_encoder_1 (
    .ADD(add), .ADDI(addi), .SUB(sub), .MULT(mult), .MULU(mulu), .DIV(div), .DIVU(divu), .AND(\and ),
    .ANDI(andi), .OR(\or ), .ORI(ori), .XOR(\xor ), .XORI(xori), .NOR(\nor ), .SLT(slt), .SLTI(slti),
    .SLTU(sltu), .SLTIU(sltiu), .Type_I(Arit_I), .ALU_SELECTOR(ALU_Slc));
  Comparator #(.width(6)) comparator_45 (.a(in_1), .b(6'b000001), .eq(j));  // open: gt, lt

  // Other names for the same wires on the sheet: _00_0000 = Especial; _11_1000 = Pila; Aritmetica = Arit;
  //   Func_Code[5:0] = in_2; lw = Load_Word; Op_Code[5:0] = in_1; NF = in_4; Rs__0 = in_4; EQF = in_5;
  //   Rs____Rt_t = in_5; sw = Store_Word; ZF = in_3

  // Notes on the sheet:
  //   Operation Decoder
  //   Aritmeticas
  //   Branch Control Selector
  //   Logicas
  //   Instrucciones Tipo R:
  //   Comparacion
  //   Copia de Registros
  //   Salto
  //   Especiales
  //   Memoria
  //   Aritmeticas
  //   Logicas
  //   Comparacion
  //   Instrucciones Tipo I:
  //   Salto
  //   Memoria
  //   Instrucciones Tipo J:
  //   Salto
endmodule

module Data_Path (
  input  Clock,
  input  Reset,
  input  Instruction_Enable,
  input  Read_Write,
  input  ALU_Result_Enable,
  input  [6:0] KBD_ASCII_Data,
  input  [1:0] Adress_Selector,
  input  Value_Selector,
  input  KBD_available,
  input  [31:0] RamData,
  input  [1:0] Selector_Destination_Adress,
  input  ALU_Selector_A,
  input  [2:0] Selector_Data,
  input  [3:0] ALU_Selector,
  input  [1:0] ALU_Selector_B,
  input  Selector_Extend,
  input  PC_Enable,
  input  [1:0] Branch_Selector,
  output [5:0] Op_Code,
  output [5:0] Func_Code,
  output [31:0] Adress,
  output [6:0] TTY_DATA,
  output [31:0] Value,
  output ZF,
  output NF,
  output EQF
);

  wire [4:0] instruction_decoder_1_out_4, multiplexer_5_out, Rd, Rt;
  wire [15:0] Constante;
  wire [25:0] Destino_Salto;
  wire [31:0] ALU, alu_1_alu_output, bit_extender_1_out, bit_extender_2_out, bit_extender_3_out,
       branch_control_1_pc_star, Data, Hi, KBD, Lo, multiplexer_1_out, multiplexer_2_out, multiplexer_3_out,
       multiplexer_6_out, PC, Random_Generator, register_1_q, RT_t, Sp;
  wire [31:7] RS;

  Random #(.width(32)) u_Random_Generator (.clk(Clock), .next(Clock), .out(Random_Generator));  // open: clr
  Multiplexer #(.select(2), .width(32), .enable("false")) multiplexer_1 (
    .in0(RT_t), .in1(32'h4), .in2(multiplexer_3_out), .out(multiplexer_1_out), .sel(ALU_Selector_B));  // open: in3
  assign bit_extender_1_out = {{16{Constante[15]}}, Constante};  // Bit_Extender bit_extender_1
  Multiplexer #(.width(32), .enable("false")) multiplexer_2 (
    .in0({RS, TTY_DATA}), .in1(Sp), .out(multiplexer_2_out), .sel(ALU_Selector_A));
  Multiplexer #(.width(32), .enable("false")) multiplexer_3 (
    .in0(bit_extender_1_out), .in1(bit_extender_2_out), .out(multiplexer_3_out), .sel(Selector_Extend));
  assign bit_extender_2_out = {{16{1'b0}}, Constante};  // Bit_Extender bit_extender_2
  Register #(.width(32)) register_1 (.D(RamData), .en(Instruction_Enable), .Q(register_1_q), .clk(Clock), .clr(Reset));
  Register #(.width(32)) register_2 (.D(RamData), .en(Clock), .Q(Data), .clk(Clock), .clr(Reset));
  ALU alu_1 (
    .in_1(Clock), .in_2(ALU_Selector), .in_3(multiplexer_2_out), .in_4(multiplexer_1_out),
    .ALU_OUTPUT(alu_1_alu_output), .ZF(ZF), .SF(NF), .out_8(EQF), .out_9(Hi), .out_10(Lo));
  Register #(.width(32)) register_3 (.D(alu_1_alu_output), .en(ALU_Result_Enable), .Q(ALU), .clk(Clock), .clr(Reset));
  assign bit_extender_3_out = {{25{1'b0}}, KBD_ASCII_Data};  // Bit_Extender bit_extender_3
  Multiplexer #(.width(32), .enable("false")) multiplexer_4 (
    .in0({32{1'b1}}), .in1(bit_extender_3_out), .out(KBD), .sel(KBD_available));
  Instruction_Decoder instruction_decoder_1 (
    .Instruction(register_1_q), .out_2(Op_Code), .out_3(Destino_Salto), .out_4(instruction_decoder_1_out_4),
    .out_5(Rt), .out_6(Constante), .out_7(Rd), .out_9(Func_Code));  // open: out_8
  Multiplexer #(.select(2), .width(5), .enable("false")) multiplexer_5 (
    .in0(Rd), .in1(Rt), .in2({5{1'b1}}), .out(multiplexer_5_out), .sel(Selector_Destination_Adress));  // open: in3
  Multiplexer #(.select(3), .width(32), .enable("false")) multiplexer_6 (
    .in0(ALU), .in1(Data), .in2(Hi), .in3(Lo), .in4(Random_Generator), .in5(KBD), .out(multiplexer_6_out),
    .sel(Selector_Data));  // open: in6, in7
  Branch_Control branch_control_1 (
    .in_1(PC), .in_2(Constante), .in_3(Destino_Salto), .in_4({RS, TTY_DATA}), .in_5(Branch_Selector),
    .PC_star(branch_control_1_pc_star));
  Multiplexer #(.select(2), .width(32), .enable("false")) multiplexer_7 (
    .in0(PC), .in1(ALU), .in2(Sp), .in3({RS, TTY_DATA}), .out(Adress), .sel(Adress_Selector));
  Program_Counter program_counter_1 (
    .in_1(branch_control_1_pc_star), .PC_Enable(PC_Enable), .CLK(Clock), .PC_Reset(Reset), .out_5(PC));
  // Register_File register_file_1: pin names not known; wires that end beside it: instruction_decoder_1_out_4, Rt, multiplexer_5_out, multiplexer_6_out, Clock, Reset, Read_Write, Sp, {RS, TTY_DATA}, RT_t
  Multiplexer #(.width(32), .enable("false")) multiplexer_8 (
    .in0({RS, TTY_DATA}), .in1(RT_t), .out(Value), .sel(Value_Selector));

  // Other names for the same wires on the sheet: Func[5:0] = Func_Code; Op[5:0] = Op_Code; RS[6:0] = TTY_DATA

  // Notes on the sheet:
  //   Data Path
  //   ALU
endmodule

module Register_File (
  input  Read_Write,
  input  Clock,
  input  Reset,
  input  [31:0] Data_Input,
  input  [4:0] Destination_Adress,
  input  [31:0] Out_A,
  input  [31:0] Out_B,
  input  [4:0] Selector_B,
  input  [4:0] Selector_A,
  input  [31:0] SP
);

  wire Input_0, Input_1, Input_2, Input_3, Input_4, Input_5, Input_6, Input_7, Input_8, Input_9, Input_10,
       Input_11, Input_12, Input_13, Input_14, Input_15, Input_16, Input_17, Input_18, Input_19, Input_20,
       Input_21, Input_22, Input_23, Input_24, Input_25, Input_26, Input_27, Input_28, Input_29, Input_30,
       Input_31;
  wire [31:0] R0, R1, R2, R3, R4, R5, R6, R7, R8, R9, R10, R11, R12, R13, R14, R15, R16, R17, R18, R19, R20,
       R21, R22, R23, R24, R25, R26, R27, R28, R29, R30;

  Demultiplexer #(.select(5), .enable("false")) demultiplexer_1 (
    .out0(Input_0), .out1(Input_1), .out2(Input_2), .out3(Input_3), .out4(Input_4), .out5(Input_5),
    .out6(Input_6), .out7(Input_7), .out8(Input_8), .out9(Input_9), .out10(Input_10), .out11(Input_11),
    .out12(Input_12), .out13(Input_13), .out14(Input_14), .out15(Input_15), .out16(Input_16),
    .out17(Input_17), .out18(Input_18), .out19(Input_19), .out20(Input_20), .out21(Input_21),
    .out22(Input_22), .out23(Input_23), .out24(Input_24), .out25(Input_25), .out26(Input_26),
    .out27(Input_27), .out28(Input_28), .out29(Input_29), .out30(Input_30), .out31(Input_31),
    .in(Read_Write), .sel(Destination_Adress));
  Register #(.width(32)) u_R0 (.D({32{1'b0}}), .en(Input_0), .Q(R0), .clk(Clock), .clr(Reset));
  Register #(.width(32)) u_R1 (.D(Data_Input), .en(Input_1), .Q(R1), .clk(Clock), .clr(Reset));
  Register #(.width(32)) u_R2 (.D(Data_Input), .en(Input_2), .Q(R2), .clk(Clock), .clr(Reset));
  Register #(.width(32)) u_R3 (.D(Data_Input), .en(Input_3), .Q(R3), .clk(Clock), .clr(Reset));
  Register #(.width(32)) u_R4 (.D(Data_Input), .en(Input_4), .Q(R4), .clk(Clock), .clr(Reset));
  Multiplexer #(.select(5), .width(32), .enable("false")) multiplexer_1 (
    .in0(R0), .in1(R1), .in2(R2), .in3(R3), .in4(R4), .in5(R5), .in6(R6), .in7(R7), .in8(R8), .in9(R9),
    .in10(R10), .in11(R11), .in12(R12), .in13(R13), .in14(R14), .in15(R15), .in16(R16), .in17(R17),
    .in18(R18), .in19(R19), .in20(R20), .in21(R21), .in22(R22), .in23(R23), .in24(R24), .in25(R25),
    .in26(R26), .in27(R27), .in28(R28), .in29(R29), .in30(R30), .in31(SP), .out(Out_A), .sel(Selector_A));
  Register #(.width(32)) u_R5 (.D(Data_Input), .en(Input_5), .Q(R5), .clk(Clock), .clr(Reset));
  Register #(.width(32)) u_R6 (.D(Data_Input), .en(Input_6), .Q(R6), .clk(Clock), .clr(Reset));
  Register #(.width(32)) u_R7 (.D(Data_Input), .en(Input_7), .Q(R7), .clk(Clock), .clr(Reset));
  Register #(.width(32)) u_R8 (.D(Data_Input), .en(Input_8), .Q(R8), .clk(Clock), .clr(Reset));
  Register #(.width(32)) u_R9 (.D(Data_Input), .en(Input_9), .Q(R9), .clk(Clock), .clr(Reset));
  Register #(.width(32)) u_R10 (.D(Data_Input), .en(Input_10), .Q(R10), .clk(Clock), .clr(Reset));
  Register #(.width(32)) u_R11 (.D(Data_Input), .en(Input_11), .Q(R11), .clk(Clock), .clr(Reset));
  Register #(.width(32)) u_R12 (.D(Data_Input), .en(Input_12), .Q(R12), .clk(Clock), .clr(Reset));
  Register #(.width(32)) u_R13 (.D(Data_Input), .en(Input_13), .Q(R13), .clk(Clock), .clr(Reset));
  Register #(.width(32)) u_R14 (.D(Data_Input), .en(Input_14), .Q(R14), .clk(Clock), .clr(Reset));
  Register #(.width(32)) u_R15 (.D(Data_Input), .en(Input_15), .Q(R15), .clk(Clock), .clr(Reset));
  Register #(.width(32)) u_R16 (.D(Data_Input), .en(Input_16), .Q(R16), .clk(Clock), .clr(Reset));
  Register #(.width(32)) u_R17 (.D(Data_Input), .en(Input_17), .Q(R17), .clk(Clock), .clr(Reset));
  Register #(.width(32)) u_R18 (.D(Data_Input), .en(Input_18), .Q(R18), .clk(Clock), .clr(Reset));
  Register #(.width(32)) u_R19 (.D(Data_Input), .en(Input_19), .Q(R19), .clk(Clock), .clr(Reset));
  Register #(.width(32)) u_R20 (.D(Data_Input), .en(Input_20), .Q(R20), .clk(Clock), .clr(Reset));
  Register #(.width(32)) u_R21 (.D(Data_Input), .en(Input_21), .Q(R21), .clk(Clock), .clr(Reset));
  Register #(.width(32)) u_R22 (.D(Data_Input), .en(Input_22), .Q(R22), .clk(Clock), .clr(Reset));
  Register #(.width(32)) u_R23 (.D(Data_Input), .en(Input_23), .Q(R23), .clk(Clock), .clr(Reset));
  Register #(.width(32)) u_R24 (.D(Data_Input), .en(Input_24), .Q(R24), .clk(Clock), .clr(Reset));
  Register #(.width(32)) u_R25 (.D(Data_Input), .en(Input_25), .Q(R25), .clk(Clock), .clr(Reset));
  Register #(.width(32)) u_R26 (.D(Data_Input), .en(Input_26), .Q(R26), .clk(Clock), .clr(Reset));
  Register #(.width(32)) u_R27 (.D(Data_Input), .en(Input_27), .Q(R27), .clk(Clock), .clr(Reset));
  Register #(.width(32)) u_R28 (.D(Data_Input), .en(Input_28), .Q(R28), .clk(Clock), .clr(Reset));
  Register #(.width(32)) u_R29 (.D(Data_Input), .en(Input_29), .Q(R29), .clk(Clock), .clr(Reset));
  Register #(.width(32)) u_R30 (.D(Data_Input), .en(Input_30), .Q(R30), .clk(Clock), .clr(Reset));
  Register #(.width(32)) R29_2 (.D(Data_Input), .en(Input_31), .Q(SP), .clk(Clock), .clr(Reset));
  Multiplexer #(.select(5), .width(32), .enable("false")) multiplexer_2 (
    .in0(R0), .in1(R1), .in2(R2), .in3(R3), .in4(R4), .in5(R5), .in6(R6), .in7(R7), .in8(R8), .in9(R9),
    .in10(R10), .in11(R11), .in12(R12), .in13(R13), .in14(R14), .in15(R15), .in16(R16), .in17(R17),
    .in18(R18), .in19(R19), .in20(R20), .in21(R21), .in22(R22), .in23(R23), .in24(R24), .in25(R25),
    .in26(R26), .in27(R27), .in28(R28), .in29(R29), .in30(R30), .in31(SP), .out(Out_B), .sel(Selector_B));

  // Other names for the same wires on the sheet: Data[31:0] = Data_Input; Destination[4:0] = Destination_Adress;
  //   R31[31:0] = SP; ReadWrite = Read_Write

  // Notes on the sheet:
  //   Register File
endmodule

module Branch_Control (
  input  [31:0] in_1,
  input  [15:0] in_2,
  input  [25:0] in_3,
  input  [31:0] in_4,
  input  [1:0] in_5,
  output [31:0] PC_star
);

  wire [15:0] multiplier_1_out;
  wire [31:0] bit_extender_1_out, PC__4, PC__4_Offset_4;

  Adder #(.width(32)) adder_1 (.a(in_1), .b(32'h4), .out(PC__4));  // open: cin, cout
  Multiplier #(.width(16)) multiplier_1 (.a(in_2), .b(16'h4), .out(multiplier_1_out));  // open: cin, cout
  assign bit_extender_1_out = {{16{1'b0}}, multiplier_1_out};  // Bit_Extender bit_extender_1
  Adder #(.width(32)) adder_2 (.a(PC__4), .b(bit_extender_1_out), .out(PC__4_Offset_4));  // open: cin, cout
  Multiplexer #(.select(2), .width(32), .enable("false")) multiplexer_1 (
    .in0(PC__4), .in1(PC__4_Offset_4), .in2({in_1[31:28], in_3, 2'b00}), .in3(in_4), .out(PC_star), .sel(in_5));

  // Other names for the same wires on the sheet: BS[1:0] = in_5; Destino[25:0] = in_3;
  //   Jump[31:2] = {in_1[31:28], in_3}; PC[31:0] = in_1; Offset[15:0] = in_2; Rs[31:0] = in_4

  // Notes on the sheet:
  //   Branch Control
endmodule

module ALU (
  input  in_1,
  input  [3:0] in_2,
  input  [31:0] in_3,
  input  [31:0] in_4,
  output [31:0] ALU_OUTPUT,
  output ZF,
  output SF,
  output out_8,
  output [31:0] out_9,
  output [31:0] out_10
);

  wire comparator_1_lt, comparator_2_lt, ENABLE_HIGH_LOW;
  wire [1:0] SELECTOR_MUL_DIV;
  wire [31:0] ADD, AND, divider_1_out, divider_1_rem, multiplexer_1_out, multiplexer_2_out,
       multiplier_1_cout, multiplier_1_out, NOR, OR, signed_divider_1_carry_out, signed_divider_1_result,
       signed_multiplier_1_carry_out, signed_multiplier_1_result, SLT, SLTU, SUB, XOR;

  assign AND = in_3 & in_4;  // AND_Gate and_1, 32 bits wide
  assign OR = in_3 | in_4;  // OR_Gate or_1, 32 bits wide
  assign XOR = in_3 ^ in_4;  // XOR_Gate xor_1, 32 bits wide
  assign NOR = ~(in_3 | in_4);  // NOR_Gate nor_1, 32 bits wide
  Comparator #(.width(32)) comparator_1 (.a(in_3), .b(in_4), .eq(out_8), .lt(comparator_1_lt));  // open: gt
  Comparator #(.width(32), .mode("unsigned")) comparator_2 (.a(in_3), .b(in_4), .lt(comparator_2_lt));  // open: gt, eq
  Adder #(.width(32)) adder_1 (.a(in_3), .b(in_4), .out(ADD));  // open: cin, cout
  Subtractor #(.width(32)) subtractor_1 (.a(in_3), .b(in_4), .out(SUB));  // open: bin, bout
  Multiplier #(.width(32)) multiplier_1 (
    .a(in_3), .b(in_4), .out(multiplier_1_out), .cout(multiplier_1_cout));  // open: cin
  Signed_Multiplier signed_multiplier_1 (
    .A(in_3), .B(in_4), .Result(signed_multiplier_1_result), .Carry_Out(signed_multiplier_1_carry_out));
  Divider #(.width(32)) divider_1 (.a(in_3), .b(in_4), .out(divider_1_out), .rem(divider_1_rem));  // open: upper
  Signed_Divider signed_divider_1 (
    .A(in_3), .B(in_4), .Result(signed_divider_1_result), .Carry_Out(signed_divider_1_carry_out));
  assign SLT = {{31{1'b0}}, comparator_1_lt};  // Bit_Extender bit_extender_1
  assign SLTU = {{31{1'b0}}, comparator_2_lt};  // Bit_Extender bit_extender_2
  Multiplexer #(.select(2), .width(32), .enable("false")) multiplexer_1 (
    .in0(multiplier_1_cout), .in1(signed_multiplier_1_carry_out), .in2(divider_1_rem),
    .in3(signed_divider_1_carry_out), .out(multiplexer_1_out), .sel(SELECTOR_MUL_DIV));
  Multiplexer #(.select(2), .width(32), .enable("false")) multiplexer_2 (
    .in0(multiplier_1_out), .in1(signed_multiplier_1_result), .in2(divider_1_out),
    .in3(signed_divider_1_result), .out(multiplexer_2_out), .sel(SELECTOR_MUL_DIV));
  Register #(.width(32)) register_1 (.D(multiplexer_1_out), .en(ENABLE_HIGH_LOW), .Q(out_9), .clk(in_1));  // open: clr
  Register #(.width(32)) register_2 (.D(multiplexer_2_out), .en(ENABLE_HIGH_LOW), .Q(out_10), .clk(in_1));  // open: clr
  and and_2 (SELECTOR_MUL_DIV[0], in_2[3], ~in_2[2], in_2[0]);  // AND_Gate
  and and_3 (SELECTOR_MUL_DIV[1], in_2[1], ~in_2[2], in_2[3]);  // AND_Gate
  and and_4 (ENABLE_HIGH_LOW, ~in_2[2], in_2[3]);  // AND_Gate
  Multiplexer #(.select(4), .width(32), .enable("false")) multiplexer_3 (
    .in0(AND), .in1(OR), .in2(XOR), .in3(NOR), .in4(SLT), .in5(SLTU), .in6(ADD), .in7(SUB), .out(ALU_OUTPUT),
    .sel(in_2));  // open: in8, in9, in10, in11, in12, in13, in14, in15
  Comparator #(.width(32)) comparator_3 (.a(in_3), .b({32{1'b0}}), .eq(ZF), .lt(SF));  // open: gt

  // Other names for the same wires on the sheet: A[31:0] = in_3; ALU_SELECTOR[3:0] = in_2; B[31:0] = in_4; CLK = in_1;
  //   EQF = out_8; HIGH[31:0] = out_9; LOW[31:0] = out_10

  // Notes on the sheet:
  //   ALU
endmodule

module Instruction_Decoder (
  input  [31:0] Instruction,
  output [5:0] out_2,
  output [25:0] out_3,
  output [4:0] out_4,
  output [4:0] out_5,
  output [15:0] out_6,
  output [4:0] out_7,
  output [4:0] out_8,
  output [5:0] out_9
);


  assign out_2 = Instruction[31:26];
  assign out_3 = Instruction[25:0];
  assign out_4 = Instruction[25:21];
  assign out_5 = Instruction[20:16];
  assign out_6 = Instruction[15:0];
  assign out_7 = Instruction[15:11];
  assign out_8 = Instruction[10:6];
  assign out_9 = Instruction[5:0];

  // Other names for the same wires on the sheet: Constante[15:0] = Instruction[15:0];
  //   Destino_salto[25:0] = Instruction[25:0]; Func_code[5:0] = Instruction[5:0]; x[4:0] = Instruction[10:6];
  //   Rd[4:0] = Instruction[15:11]; Rt[4:0] = Instruction[20:16]; Rs[4:0] = Instruction[25:21];
  //   Op_Code[5:0] = Instruction[31:26]

  // Notes on the sheet:
  //   Instruction Decoder
endmodule

module Signed_Multiplier (
  input  [31:0] A,
  input  [31:0] B,
  output [31:0] Result,
  output [31:0] Carry_Out
);

  wire xor_1_out;
  wire [31:0] multiplexer_1_out, multiplexer_2_out, multiplier_1_out, negator_1_out, negator_2_out,
       negator_3_out;

  // Probe on A
  // Probe on B
  Negator #(.width(32)) negator_1 (.in(A), .out(negator_1_out));
  Negator #(.width(32)) negator_2 (.in(B), .out(negator_2_out));
  Multiplexer #(.width(32), .enable("false")) multiplexer_1 (
    .in0(A), .in1(negator_1_out), .out(multiplexer_1_out), .sel(A[31]));
  Multiplexer #(.width(32), .enable("false")) multiplexer_2 (
    .in0(B), .in1(negator_2_out), .out(multiplexer_2_out), .sel(B[31]));
  Multiplier #(.width(32)) multiplier_1 (
    .a(multiplexer_1_out), .b(multiplexer_2_out), .out(multiplier_1_out), .cout(Carry_Out));  // open: cin
  xor xor_1 (xor_1_out, A[31], B[31]);
  Negator #(.width(32)) negator_3 (.in(multiplier_1_out), .out(negator_3_out));
  // Probe on Carry_Out
  Multiplexer #(.width(32), .enable("false")) multiplexer_3 (
    .in0(multiplier_1_out), .in1(negator_3_out), .out(Result), .sel(xor_1_out));
  // Probe on Result

  // Notes on the sheet:
  //   Signed Multiplier
endmodule

module Signed_Divider (
  input  [31:0] A,
  input  [31:0] B,
  output [31:0] Result,
  output [31:0] Carry_Out
);

  wire xor_1_out;
  wire [31:0] divider_1_out, multiplexer_1_out, multiplexer_2_out, negator_1_out, negator_2_out,
       negator_3_out;

  // Probe on A
  // Probe on B
  Negator #(.width(32)) negator_1 (.in(A), .out(negator_1_out));
  Negator #(.width(32)) negator_2 (.in(B), .out(negator_2_out));
  Multiplexer #(.width(32), .enable("false")) multiplexer_1 (
    .in0(A), .in1(negator_1_out), .out(multiplexer_1_out), .sel(A[31]));
  Multiplexer #(.width(32), .enable("false")) multiplexer_2 (
    .in0(B), .in1(negator_2_out), .out(multiplexer_2_out), .sel(B[31]));
  Divider #(.width(32)) divider_1 (
    .a(multiplexer_1_out), .b(multiplexer_2_out), .out(divider_1_out), .rem(Carry_Out));  // open: upper
  xor xor_1 (xor_1_out, A[31], B[31]);
  Negator #(.width(32)) negator_3 (.in(divider_1_out), .out(negator_3_out));
  // Probe on Carry_Out
  Multiplexer #(.width(32), .enable("false")) multiplexer_3 (
    .in0(divider_1_out), .in1(negator_3_out), .out(Result), .sel(xor_1_out));
  // Probe on Result

  // Notes on the sheet:
  //   Signed Divider
endmodule

module ALU_Encoder (
  input  ADD,
  input  ADDI,
  input  SUB,
  input  MULT,
  input  MULU,
  input  DIV,
  input  DIVU,
  input  AND,
  input  ANDI,
  input  OR,
  input  ORI,
  input  XOR,
  input  XORI,
  input  NOR,
  input  SLT,
  input  SLTI,
  input  SLTU,
  input  SLTIU,
  output Type_I,
  output [3:0] ALU_SELECTOR
);

  wire ADD_t, AND_t, OR_t, SLT_t, SLTU_t, XOR_t;

  and and_1 (ADD_t, ADD, ADDI);
  and and_2 (AND_t, AND, ANDI);
  and and_3 (OR_t, OR, ORI);
  and and_4 (XOR_t, XOR, XORI);
  and and_5 (SLT_t, SLT, SLTI);
  and and_6 (SLTU_t, SLTU, SLTIU);
  or or_1 (Type_I, ADDI, ANDI, ORI, XORI, SLTI, SLTIU);
  or or_2 (ALU_SELECTOR[0], OR_t, NOR, SLTU_t, SUB, MULU, DIVU);
  or or_3 (ALU_SELECTOR[1], XOR_t, NOR, ADD_t, SUB, DIV, DIVU);
  or or_4 (ALU_SELECTOR[2], SLT_t, SLTU_t, ADD_t, SUB);
  or or_5 (ALU_SELECTOR[3], MULT, MULU, DIV, DIVU);

  // Notes on the sheet:
  //   ALU Encoder
endmodule

module Little_Endian_Big_Endian (
  input  [31:0] Input,
  output [31:0] out_2
);


  assign out_2 = {Input[7:0], Input[15:8], Input[23:16], Input[31:24]};
endmodule

module Program_Counter (
  input  [31:0] in_1,
  input  PC_Enable,
  input  CLK,
  input  PC_Reset,
  output [31:0] out_5
);

  Register #(.width(32)) register_1 (.D(in_1), .en(PC_Enable), .Q(out_5), .clk(CLK), .clr(PC_Reset));

  // Notes on the sheet:
  //   Program Counter
endmodule

module Timer (
  input  [3:0] in_1,
  input  in_2,
  input  CLK,
  input  Clear,
  output out_5
);

  wire [3:0] counter_1_q;

  Counter #(.width(4), .max('hf)) counter_1 (
    .count(in_2), .Q(counter_1_q), .clk(CLK), .clr(Clear));  // open: load, D, carry
  Comparator #(.width(4)) comparator_1 (.a(in_1), .b(counter_1_q), .eq(out_5));  // open: gt, lt

  // Notes on the sheet:
  //   Timer
endmodule
